# Fritzing sketch 1-2-runningLED (saved by Fritzing 0.9.6b)
breadboards: 1

parts:
  LED4 = LED - 5mm [color="Red (633nm)" current=0.030 package="5 mm [THT]"]
  LED3 = LED - 5mm [color="Red (633nm)" current=0.030 package="5 mm [THT]"]
  LED2 = LED - 5mm [color="Red (633nm)" current=0.030 package="5 mm [THT]"]
  LED7 = LED - 5mm [color="Red (633nm)" current=0.030 package="5 mm [THT]"]
  LED6 = LED - 5mm [color="Red (633nm)" current=0.030 package="5 mm [THT]"]
  LED1 = LED - 5mm [color="Red (633nm)" current=0.030 package="5 mm [THT]"]
  LED5 = LED - 5mm [color="Red (633nm)" current=0.030 package="5 mm [THT]"]
  LED8 = LED - 5mm [color="Red (633nm)" current=0.030 package="5 mm [THT]"]
  Arduino1 = Arduino Mega 2560 (Rev3)

nets:
  N1: LED4.cathode, Arduino1.D25
  N2: LED4.anode, LED3.anode, LED2.anode, LED7.anode, LED6.anode, LED1.anode, LED5.anode, LED8.anode, Arduino1.5V
  N3: LED3.cathode, Arduino1.D24
  N4: LED2.cathode, Arduino1.D23
  N5: LED7.cathode, Arduino1.D28
  N6: LED6.cathode, Arduino1.D27
  N7: LED1.cathode, Arduino1.D22
  N8: LED5.cathode, Arduino1.D26
  N9: LED8.cathode, Arduino1.D29

notes:
  BLINK

// code stored in the sketch: Blink.ino
/*
  Blink
  
  Switching a LED on and off
  
  This example is part of the Fritzing Creator Kit: www.fritzing.org/creator-kit.
*/

int led = 13;                   // integer variable led is declared

void setup() {                  // the setup() method is executed only once
  pinMode(led, OUTPUT);         // the led PIN is declared as digital output
}

void loop() {                   // the loop() method is repeated
  digitalWrite(led, HIGH);      // switching on the led 
  delay(1000);                  // stopping the program for 1000 milliseconds
  digitalWrite(led, LOW);       // switching off the led 
  delay(1000);                  // stopping the program for 1000 milliseconds
}
