# Fritzing sketch 2-4-Multipleinterrupt (saved by Fritzing 0.9.6b)
breadboards: 1

parts:
  LED4 = LED - 5mm [color="Red (633nm)" current=0.030 package="5 mm [THT]"]
  LED3 = LED - 5mm [color="Red (633nm)" current=0.030 package="5 mm [THT]"]
  LED2 = LED - 5mm [color="Red (633nm)" current=0.030 package="5 mm [THT]"]
  LED7 = LED - 5mm [color="Red (633nm)" current=0.030 package="5 mm [THT]"]
  LED6 = LED - 5mm [color="Red (633nm)" current=0.030 package="5 mm [THT]"]
  LED1 = LED - 5mm [color="Red (633nm)" current=0.030 package="5 mm [THT]"]
  LED5 = LED - 5mm [color="Red (633nm)" current=0.030 package="5 mm [THT]"]
  LED8 = LED - 5mm [color="Red (633nm)" current=0.030 package="5 mm [THT]"]
  Arduino1 = Arduino Mega 2560 (Rev3)
  R1 = Resistor [tolerance=±5% power=0.25 resistance=220 package=THT]
  R2 = Resistor [tolerance=±5% power=0.25 resistance=220 package=THT]
  R3 = Resistor [tolerance=±5% power=0.25 resistance=220 package=THT]
  R4 = Resistor [tolerance=±5% power=0.25 resistance=220 package=THT]
  R5 = Resistor [tolerance=±5% power=0.25 resistance=220 package=THT]
  R6 = Resistor [tolerance=±5% power=0.25 resistance=220 package=THT]
  R7 = Resistor [tolerance=±5% power=0.25 resistance=220 package=THT]
  R8 = Resistor [tolerance=±5% power=0.25 resistance=220 package=THT]
  S1 = Pushbutton [package=THT]
  LED9 = LED - 5mm [color="Red (633nm)" current=0.030 package="5 mm [THT]"]
  R9 = Resistor [tolerance=±5% power=0.25 resistance=220 package=THT]
  S2 = Pushbutton [package=THT]

nets:
  N1: LED4.cathode, Arduino1.D25
  N2: LED4.anode, R5.Pin_0
  N3: LED3.cathode, Arduino1.D24
  N4: LED3.anode, R6.Pin_0
  N5: LED2.cathode, Arduino1.D23
  N6: LED2.anode, R7.Pin_0
  N7: LED7.cathode, Arduino1.D28
  N8: LED7.anode, R2.Pin_0
  N9: LED6.cathode, Arduino1.D27
  N10: LED6.anode, R3.Pin_0
  N11: LED1.cathode, Arduino1.D22
  N12: LED1.anode, R8.Pin_0
  N13: LED5.cathode, Arduino1.D26
  N14: LED5.anode, R4.Pin_0
  N15: LED8.cathode, Arduino1.D29
  N16: LED8.anode, R1.Pin_0
  N17: Arduino1.D21/SCL, S1.leg0
  N18: Arduino1.D20/SDA, S2.leg0
  N19: Arduino1.GND, S1.leg1, LED9.cathode, S2.leg1
  N20: Arduino1.D13_PWM, R9.Pin_1
  N21: Arduino1.5V, R1.Pin_1, R2.Pin_1, R3.Pin_1, R4.Pin_1, R5.Pin_1, R6.Pin_1, R7.Pin_1, R8.Pin_1
  N22: LED9.anode, R9.Pin_0

notes:
  BLINK

// code stored in the sketch: Blink.ino
/*
  Blink
  
  Switching a LED on and off
  
  This example is part of the Fritzing Creator Kit: www.fritzing.org/creator-kit.
*/

int led = 13;                   // integer variable led is declared

void setup() {                  // the setup() method is executed only once
  pinMode(led, OUTPUT);         // the led PIN is declared as digital output
}

void loop() {                   // the loop() method is repeated
  digitalWrite(led, HIGH);      // switching on the led 
  delay(1000);                  // stopping the program for 1000 milliseconds
  digitalWrite(led, LOW);       // switching off the led 
  delay(1000);                  // stopping the program for 1000 milliseconds
}
